# Fritzing sketch multistepper (saved by Fritzing 0.9.3b)
circuit board: 8.46667cm x 5.64444cm
breadboards: 1

parts:
  元件1 = Arduino Uno (Rev3)
  SW1 = DIP Switch 8 Position [package=dipswitch-08]
  MD09B1 = A4988 Stepper Motor Driver Carrier
  M1 = Stepper Motor - Bipolar
  J1 = Screw terminal - 2 pins [package=THT]

nets:
  N1: 元件1.D8, SW1.5
  N2: 元件1.D9_PWM, SW1.4
  N3: 元件1.D10_PWM/SS, SW1.3
  N4: 元件1.D11_PWM/MOSI, SW1.2
  N5: 元件1.D12/MISO, SW1.1
  N6: 元件1.GND, SW1.10, SW1.11, SW1.12, SW1.13, SW1.14, SW1.15, SW1.16, MD09B1.GROUND#147
  N7: 元件1.D2, MD09B1.DIR
  N8: 元件1.D3_PWM, MD09B1.STEP
  N9: 元件1.D4, MD09B1.Enable
  N10: 元件1.D6_PWM, SW1.7
  N11: 元件1.D7, SW1.6
  5V: 元件1.5V, MD09B1.OUT_2B, MD09B1.OUT_1B, MD09B1.VDD, M1.A, M1.D
  N12: MD09B1.VMOT, J1.pin1
  N13: MD09B1.GROUND#141, J1.pin2
  N14: MD09B1.OUT_2A, M1.C
  N15: MD09B1.OUT_1A, M1.B
